# Fritzing sketch Platine_sousvide4.2 (saved by Fritzing 0.9.3b)
circuit board: 5.447cm x 6.27821cm
breadboards: 1

parts:
  ATMEGA = atmega328 [package=dip]
  Power = mystery part, 2 pins [chip_label=?]
  R1 = Resistor [tolerance=±5% resistance=4.7k package=THT]
  button = mystery part, 2 pins [chip_label=?]
  RF = mystery part, 4 pins [chip_label=?]
  Poti = mystery part, 3 pins [chip_label=?]
  R2 = Resistor [tolerance=±5% resistance=1k package=THT]
  R3 = Resistor [tolerance=±5% resistance=10k package=THT]
  R4 = Resistor [tolerance=±5% resistance=220 package=THT]
  C1 = Ceramic Capacitor [capacitance=100nF package="100 mil [THT, multilayer]"]
  LCD_1 = mystery part, 6 pins [chip_label=?]
  LCD_2 = mystery part, 6 pins [chip_label=?]
  Bluetooth = mystery part, 4 pins [chip_label=?]
  Temp = mystery part, 3 pins [chip_label=?]

nets:
  N1: ATMEGA.D0_(RX), Bluetooth.pin2
  N2: ATMEGA.D1_(TX), Bluetooth.pin1
  N3: ATMEGA.VCC, ATMEGA.AVCC, Power.pin1, R1.Pin_0, RF.pin3, Poti.pin1, R3.Pin_0, R4.Pin_1, LCD_2.pin2, Bluetooth.pin3, Temp.pin3
  N4: ATMEGA.GND, Power.pin2, button.pin1, RF.pin1, Poti.pin3, R2.Pin_1, C1.0, LCD_1.pin6, LCD_2.pin1, LCD_2.pin5, Bluetooth.pin4, Temp.pin1
  N5: ATMEGA.D5_(PWM), LCD_1.pin4
  N6: ATMEGA.D6_(PWM), LCD_1.pin3
  N7: ATMEGA.D7, LCD_1.pin2
  N8: ATMEGA.D8, LCD_1.pin1
  N9: ATMEGA.D9_(PWM), LCD_2.pin4
  N10: ATMEGA.D10_(PWM), LCD_2.pin6
  N11: ATMEGA.D11_(PWM), R1.Pin_1, Temp.pin2
  N12: ATMEGA.D12, RF.pin2
  N13: ATMEGA.D13, button.pin2
  N14: ATMEGA.AREF, C1.1
  N15: ATMEGA.A0, Poti.pin2
  N16: R2.Pin_0, R3.Pin_1, LCD_2.pin3
  N17: R4.Pin_0, LCD_1.pin5

notes:
  Sous Vide
